// Logisim project 40075 exp 6.circ as structural Verilog: 1 circuit, main circuit main
module main (
  input  in_1,
  input  in_2,
  input  in_3
);

  wire clock_1_out, d_ff_1_q, d_ff_2_q, d_ff_3_q, d_ff_4_q, xor_1_out;

  Clock clock_1 (.out(clock_1_out));
  D_Flip_Flop d_ff_1 (
    .clk(clock_1_out), .D(d_ff_2_q), .Q(d_ff_1_q), .preset(in_1), .en(in_2), .reset(in_3));  // open: Qn
  LED led_1 ();  // open: in
  D_Flip_Flop d_ff_2 (
    .clk(clock_1_out), .D(d_ff_3_q), .Q(d_ff_2_q), .preset(in_1), .en(in_2), .reset(in_3));  // open: Qn
  LED led_2 ();  // open: in
  D_Flip_Flop d_ff_3 (
    .clk(clock_1_out), .D(xor_1_out), .Q(d_ff_3_q), .preset(in_1), .en(in_2), .reset(in_3));  // open: Qn
  LED led_3 ();  // open: in
  D_Flip_Flop d_ff_4 (
    .clk(clock_1_out), .D(xor_1_out), .Q(d_ff_4_q), .preset(in_1), .en(in_2), .reset(in_3));  // open: Qn
  xor xor_1 (xor_1_out, d_ff_4_q, d_ff_1_q);
  LED led_4 ();  // open: in
endmodule
