// Logisim project 40075 exp 7.circ as structural Verilog: 1 circuit, main circuit main
module main (
  input  in_1,
  input  in_2,
  input  in_3,
  input  in_4
);

  wire clock_1_out, d_ff_1_q, d_ff_2_q, d_ff_3_q, d_ff_4_q, not_1_out, not_2_out, or_1_out;

  Clock clock_1 (.out(clock_1_out));
  D_Flip_Flop d_ff_1 (.clk(clock_1_out), .D(in_1), .Q(d_ff_1_q), .preset(in_2), .en(in_3), .reset(in_4));  // open: Qn
  D_Flip_Flop d_ff_2 (
    .clk(clock_1_out), .D(d_ff_1_q), .Q(d_ff_2_q), .preset(in_2), .en(in_3), .reset(in_4));  // open: Qn
  not not_1 (not_1_out, d_ff_2_q);
  not not_2 (not_2_out, d_ff_3_q);
  D_Flip_Flop d_ff_3 (
    .clk(clock_1_out), .D(d_ff_2_q), .Q(d_ff_3_q), .preset(in_2), .en(in_3), .reset(in_4));  // open: Qn
  D_Flip_Flop d_ff_4 (
    .clk(clock_1_out), .D(d_ff_3_q), .Q(d_ff_4_q), .preset(in_2), .en(in_3), .reset(in_4));  // open: Qn
  or or_1 (or_1_out, d_ff_1_q, not_1_out, not_2_out, d_ff_4_q);
  LED led_1 (.in(or_1_out));
endmodule
