// Logisim project 40075 exp 8.circ as structural Verilog: 1 circuit, main circuit main
module main (
  input  [7:0] in_1,
  input  [7:0] in_2,
  input  [7:0] in_3,
  input  [2:0] in_4,
  input  [2:0] in_5,
  output out_6,
  output out_7,
  output [7:0] out_8
);

  wire [2:0] undriven;
  wire [7:0] adder_1_out, and_1_out, multiplier_1_out, or_1_out, shifter_1_out, shifter_2_out,
       subtractor_1_out, xor_1_out;

  Subtractor subtractor_1 (.a(in_1), .b(in_2), .out(subtractor_1_out), .bout(out_7));  // open: bin
  Multiplier multiplier_1 (.a(in_1), .b(in_2), .out(multiplier_1_out), .cout(in_3));  // open: cin
  assign and_1_out = in_1;  // AND_Gate and_1, 8 bits wide AND_Gate
  assign or_1_out = in_1 | in_2;  // OR_Gate or_1, 8 bits wide
  assign xor_1_out = in_1 ^ in_2;  // XOR_Gate xor_1, 8 bits wide
  Shifter #(.shift("lr")) shifter_1 (.in(in_2), .\dist (in_5), .out(shifter_1_out));
  Shifter #(.shift("rl")) shifter_2 (.in(in_2), .\dist (in_5), .out(shifter_2_out));
  Adder adder_1 (.a(in_1), .b(in_2), .out(adder_1_out), .cout(out_6));  // open: cin
  Multiplexer #(.select(3), .width(8), .enable("false")) multiplexer_1 (
    .in0(adder_1_out), .in1(subtractor_1_out), .in2(multiplier_1_out), .in3(and_1_out), .in4(or_1_out),
    .in5(xor_1_out), .in7(shifter_1_out), .out(out_8), .sel(undriven));  // open: in6
endmodule
