// Logisim project exp 5.circ as structural Verilog: 1 circuit, main circuit main
module main (
  input  in_1,
  input  in_2,
  input  in_3
);

  _7_Segment_Display u_7_segment_display_1 (.g(in_1), .f(in_1), .a(in_1), .e(in_1), .d(in_1), .dp(in_1));  // open: b, c
  _7_Segment_Display u_7_segment_display_2 (.f(in_2), .a(in_2), .e(in_2), .d(in_2), .dp(in_2));  // open: g, b, c
  _7_Segment_Display u_7_segment_display_3 (.g(in_3), .f(in_3), .a(in_3), .e(in_3), .d(in_3));  // open: b, c, dp
endmodule
