// Logisim project expppppppppp 12.circ as structural Verilog: 1 circuit, main circuit main
module main (
  input  in_1,
  input  in_2,
  input  in_3,
  input  in_4,
  input  [3:0] in_5,
  input  [3:0] in_6,
  input  [3:0] in_7,
  input  [3:0] in_8,
  output [3:0] out_9,
  output out_10,
  output out_11,
  output [3:0] out_12,
  output out_13,
  output out_14,
  output [3:0] out_15,
  output out_16,
  output out_17,
  output out_18,
  output [3:0] out_19,
  output out_20
);

  wire clock_1_out, comparator_1_eq, comparator_2_eq, comparator_3_eq, comparator_4_eq, not_1_out, not_2_out,
       not_3_out, not_4_out;

  not not_1 (not_1_out, in_1);
  not not_2 (not_2_out, in_3);
  not not_3 (not_3_out, in_2);
  not not_4 (not_4_out, in_4);
  and and_1 (out_10, in_1, not_3_out, not_2_out, not_4_out);
  and and_2 (out_13, not_1_out, in_2, not_2_out, not_4_out);
  and and_3 (out_16, not_1_out, not_3_out, in_3, not_4_out);
  and and_4 (out_18, not_1_out, not_3_out, not_2_out, in_4);
  Clock clock_1 (.out(clock_1_out));
  Register #(.width(4)) register_1 (.Q(out_9), .clk(clock_1_out));  // open: D, en, clr
  Register #(.width(4)) register_2 (.Q(out_12), .clk(clock_1_out));  // open: D, en, clr
  Register #(.width(4)) register_3 (.Q(out_15), .clk(clock_1_out));  // open: D, en, clr
  Register #(.width(4)) register_4 (.Q(out_19), .clk(clock_1_out));  // open: D, en, clr
  Comparator #(.width(4)) comparator_1 (.a(out_9), .b(in_5), .eq(comparator_1_eq));  // open: gt, lt
  Comparator #(.width(4)) comparator_2 (.a(out_12), .b(in_6), .eq(comparator_2_eq));  // open: gt, lt
  Comparator #(.width(4)) comparator_3 (.a(out_15), .b(in_7), .eq(comparator_3_eq));  // open: gt, lt
  Comparator #(.width(4)) comparator_4 (.a(out_19), .b(in_8), .eq(comparator_4_eq));  // open: gt, lt
  and and_5 (out_11, out_10, comparator_1_eq);
  and and_6 (out_14, out_13, comparator_2_eq);
  and and_7 (out_17, out_16, comparator_3_eq);
  and and_8 (out_20, out_18, comparator_4_eq);
endmodule
