// Logisim project expppppppppp 8.circ as structural Verilog: 1 circuit, main circuit main
module main (
  input  [7:0] in_1,
  input  [7:0] in_2,
  input  [2:0] in_3,
  input  [2:0] in_4,
  output out_5,
  output out_6,
  output [7:0] out_7,
  output [7:0] out_8
);

  wire [2:0] undriven_2;
  wire [7:0] adder_1_out, and_1_out, multiplier_1_out, or_1_out, shifter_1_out, shifter_2_out,
       subtractor_1_out, undriven, xor_1_out;

  Adder adder_1 (.a(in_1), .b(undriven), .out(adder_1_out), .cout(out_5));  // open: cin
  Subtractor subtractor_1 (.a(in_1), .b(undriven), .out(subtractor_1_out), .bout(out_6));  // open: bin
  Multiplier multiplier_1 (.a(in_1), .b(undriven), .out(multiplier_1_out), .cout(out_7));  // open: cin
  assign and_1_out = in_1 & undriven;  // AND_Gate and_1, 8 bits wide
  assign or_1_out = in_1 | undriven;  // OR_Gate or_1, 8 bits wide
  assign xor_1_out = in_1 ^ undriven;  // XOR_Gate xor_1, 8 bits wide
  Shifter #(.shift("lr")) shifter_1 (.in(in_1), .\dist (in_4), .out(shifter_1_out));
  Shifter #(.shift("rl")) shifter_2 (.in(in_1), .\dist (in_4), .out(shifter_2_out));
  Multiplexer #(.select(3), .width(8), .enable("false")) multiplexer_1 (
    .in0(adder_1_out), .in1(subtractor_1_out), .in2(multiplier_1_out), .in3(and_1_out), .in4(or_1_out),
    .in5(xor_1_out), .in6(shifter_1_out), .out(out_8), .sel(undriven_2));  // open: in7
endmodule
