// Logisim project expppppppppp 9.circ as structural Verilog: 1 circuit, main circuit main
module main (
  input  [3:0] in_1,
  input  [3:0] in_2,
  input  [3:0] in_3,
  input  [1:0] in_4,
  input  [1:0] in_5,
  input  [3:0] in_6,
  input  in_7,
  input  in_8,
  output [3:0] out_9,
  output [3:0] out_10,
  output [3:0] out_11,
  output [3:0] out_12,
  output [3:0] out_13,
  output [3:0] out_14,
  output [3:0] out_15,
  output [3:0] out_16
);

  wire clock_1_out, demultiplexer_2_out0, demultiplexer_2_out1, demultiplexer_2_out2, demultiplexer_2_out3;
  wire [1:0] undriven, undriven_2;
  wire [3:0] demultiplexer_1_out0, demultiplexer_1_out1, demultiplexer_1_out2, demultiplexer_1_out3,
       multiplexer_1_out;

  Clock clock_1 (.out(clock_1_out));
  Register #(.width(4)) register_1 (.D(in_1), .Q(out_9), .clk(clock_1_out), .clr(in_7));  // open: en
  Register #(.width(4)) register_2 (.D(in_2), .Q(out_11), .clk(clock_1_out), .clr(in_7));  // open: en
  Register #(.width(4)) register_3 (.D(in_3), .Q(out_13), .clk(clock_1_out), .clr(in_7));  // open: en
  Register #(.width(4)) register_4 (.D(in_6), .Q(out_15), .clk(clock_1_out), .clr(in_7));  // open: en
  Multiplexer #(.select(2), .width(4), .enable("false")) multiplexer_1 (
    .in0(out_9), .in1(out_11), .in2(out_13), .in3(out_15), .out(multiplexer_1_out), .sel(undriven));
  Demultiplexer #(.select(2), .width(4), .enable("false")) demultiplexer_1 (
    .out0(demultiplexer_1_out0), .out1(demultiplexer_1_out1), .out2(demultiplexer_1_out2),
    .out3(demultiplexer_1_out3), .in(multiplexer_1_out), .sel(undriven_2));
  Demultiplexer #(.select(2), .enable("false")) demultiplexer_2 (
    .out0(demultiplexer_2_out0), .out1(demultiplexer_2_out1), .out2(demultiplexer_2_out2),
    .out3(demultiplexer_2_out3), .in(in_8), .sel(undriven_2));
  Register #(.width(4)) register_5 (
    .D(demultiplexer_1_out0), .en(demultiplexer_2_out0), .Q(out_10), .clk(clock_1_out));  // open: clr
  Register #(.width(4)) register_6 (
    .D(demultiplexer_1_out1), .en(demultiplexer_2_out1), .Q(out_12), .clk(clock_1_out));  // open: clr
  Register #(.width(4)) register_7 (
    .D(demultiplexer_1_out2), .en(demultiplexer_2_out2), .Q(out_14), .clk(clock_1_out));  // open: clr
  Register #(.width(4)) register_8 (
    .D(demultiplexer_1_out3), .en(demultiplexer_2_out3), .Q(out_16), .clk(clock_1_out));  // open: clr
endmodule
